// Logisim project main.circ as structural Verilog: 7 circuits, main circuit Datapath
module Datapath (
  input  Clock,
  input  Clear,
  output [17:0] Read_Data2,
  output [17:0] Read_Data1
);

  wire alu_1_zero, and_1_out, controlunitupdated_1_alusrc, controlunitupdated_1_branch,
       controlunitupdated_1_memread, controlunitupdated_1_memtoreg, controlunitupdated_1_memwrite,
       controlunitupdated_1_regdst, controlunitupdated_1_regwrite;
  wire [1:0] controlunitupdated_1_aluop2;
  wire [2:0] alucontrolupdated_1_op;
  wire [3:0] adder_1_out, multiplexer_1_out, multiplexer_3_out, PC_q;
  wire [17:0] alu_1_result, bit_extender_1_out, multiplexer_2_out, multiplexer_4_out, ram_1_data,
       registerfile_1_read_register1_rs_2, registerfile_1_read_register2_rt_2, rom_1_data;

  Register #(.width(4)) PC (.D(multiplexer_3_out), .Q(PC_q), .clk(Clock), .clr(Clear));  // open: en
  Adder #(.width(4)) adder_1 (.a(4'b0001), .b(PC_q), .out(adder_1_out));  // open: cin, cout
  ROM #(.addrWidth(4), .dataWidth(18)) rom_1 (.addr(PC_q), .data(rom_1_data));  // open: sel
  assign bit_extender_1_out = {{12{1'b0}}, rom_1_data[5:0]};  // Bit_Extender bit_extender_1
  Multiplexer #(.width(4), .enable("false")) multiplexer_1 (
    .in0(rom_1_data[9:6]), .in1(rom_1_data[5:2]), .out(multiplexer_1_out), .sel(controlunitupdated_1_regdst));
  RegisterFile registerfile_1 (
    .Read_Register1_RS(rom_1_data[13:10]), .Read_Register2_RT(rom_1_data[9:6]),
    .RegWrite(controlunitupdated_1_regwrite), .Clock(Clock), .Write_Data(multiplexer_4_out),
    .Read_Register1_RS_2(registerfile_1_read_register1_rs_2),
    .Read_Register2_RT_2(registerfile_1_read_register2_rt_2), .Write_Register(multiplexer_1_out));  // open: Clear
  ALUControlUpdated alucontrolupdated_1 (
    .ALUop(controlunitupdated_1_aluop2), .Func(rom_1_data[1:0]), .Op(alucontrolupdated_1_op));
  Multiplexer #(.width(18), .enable("false")) multiplexer_2 (
    .in0(registerfile_1_read_register2_rt_2), .in1(bit_extender_1_out), .out(multiplexer_2_out),
    .sel(controlunitupdated_1_alusrc));
  ControlUnitUpdated controlunitupdated_1 (
    .Opcode(rom_1_data[17:14]), .RegDst(controlunitupdated_1_regdst), .ALUSrc(controlunitupdated_1_alusrc),
    .MemtoReg(controlunitupdated_1_memtoreg), .RegWrite(controlunitupdated_1_regwrite),
    .MemRead(controlunitupdated_1_memread), .MemWrite(controlunitupdated_1_memwrite),
    .Branch(controlunitupdated_1_branch), .ALUop1(controlunitupdated_1_aluop2[1]),
    .ALUop2(controlunitupdated_1_aluop2[0]));
  ALU alu_1 (
    .A(registerfile_1_read_register1_rs_2), .B(multiplexer_2_out), .Result(alu_1_result), .Zero(alu_1_zero),
    .Opcode(alucontrolupdated_1_op));
  Multiplexer #(.width(4), .enable("false")) multiplexer_3 (
    .in0(adder_1_out), .out(multiplexer_3_out), .sel(and_1_out));  // open: in1
  and and_1 (and_1_out, controlunitupdated_1_branch, alu_1_zero);
  Multiplexer #(.width(18), .enable("false")) multiplexer_4 (
    .in0(alu_1_result), .in1(ram_1_data), .out(multiplexer_4_out), .sel(controlunitupdated_1_memtoreg));
  RAM #(.addrWidth(18), .dataWidth(18), .bus("separate")) ram_1 (
    .addr(alu_1_result), .din(registerfile_1_read_register2_rt_2), .data(ram_1_data),
    .str(controlunitupdated_1_memwrite), .clk(Clock), .ld(controlunitupdated_1_memread));  // open: sel, clr

  // Notes on the sheet:
  //   contents of rom_1 (hex, n*v repeats v):
  //   0 14c8 10047 14080
  //   RegDst
  //   ALUSrc
  //   PCSrc
  //   MemToReg
endmodule

module RegisterFile (
  input  [3:0] Read_Register1_RS,
  input  [3:0] Read_Register2_RT,
  input  [3:0] Write_Register,
  input  RegWrite,
  input  Clock,
  input  [17:0] Write_Data,
  input  Clear,
  output [17:0] Read_Register1_RS_2,
  output [17:0] Read_Register2_RT_2
);

  wire and_1_out, and_2_out, and_3_out, and_4_out, and_5_out, and_6_out, and_7_out, and_8_out, and_9_out,
       and_10_out, and_11_out, and_12_out, and_13_out, and_14_out, and_15_out, and_16_out, decoder_1_out0,
       decoder_1_out1, decoder_1_out2, decoder_1_out3, decoder_1_out4, decoder_1_out5, decoder_1_out6,
       decoder_1_out7, decoder_1_out8, decoder_1_out9, decoder_1_out10, decoder_1_out11, decoder_1_out12,
       decoder_1_out13, decoder_1_out14, decoder_1_out15;
  wire [17:0] _0_q, _1_q, _2_q, _3_q, _4_q, _5_q, _6_q, _7_q, _8_q, _9_q, _10_q, _11_q, _12_q, _13_q, _14_q,
       _15_q;

  Decoder #(.select(4), .enable("false")) decoder_1 (
    .out0(decoder_1_out0), .out1(decoder_1_out1), .out2(decoder_1_out2), .out3(decoder_1_out3),
    .out4(decoder_1_out4), .out5(decoder_1_out5), .out6(decoder_1_out6), .out7(decoder_1_out7),
    .out8(decoder_1_out8), .out9(decoder_1_out9), .out10(decoder_1_out10), .out11(decoder_1_out11),
    .out12(decoder_1_out12), .out13(decoder_1_out13), .out14(decoder_1_out14), .out15(decoder_1_out15),
    .sel(Write_Register));
  Register #(.width(18)) _0 (.D(Write_Data), .en(and_1_out), .Q(_0_q), .clk(Clock), .clr(Clear));
  and and_1 (and_1_out, decoder_1_out0, RegWrite);
  Register #(.width(18)) _1 (.D(Write_Data), .en(and_2_out), .Q(_1_q), .clk(Clock), .clr(Clear));
  and and_2 (and_2_out, decoder_1_out1, RegWrite);
  Register #(.width(18)) _2 (.D(Write_Data), .en(and_3_out), .Q(_2_q), .clk(Clock), .clr(Clear));
  and and_3 (and_3_out, decoder_1_out2, RegWrite);
  Register #(.width(18)) _3 (.D(Write_Data), .en(and_4_out), .Q(_3_q), .clk(Clock), .clr(Clear));
  and and_4 (and_4_out, decoder_1_out3, RegWrite);
  Register #(.width(18)) _4 (.D(Write_Data), .en(and_5_out), .Q(_4_q), .clk(Clock), .clr(Clear));
  and and_5 (and_5_out, decoder_1_out4, RegWrite);
  Register #(.width(18)) _5 (.D(Write_Data), .en(and_6_out), .Q(_5_q), .clk(Clock), .clr(Clear));
  and and_6 (and_6_out, decoder_1_out5, RegWrite);
  Register #(.width(18)) _6 (.D(Write_Data), .en(and_7_out), .Q(_6_q), .clk(Clock), .clr(Clear));
  and and_7 (and_7_out, decoder_1_out6, RegWrite);
  Register #(.width(18)) _7 (.D(Write_Data), .en(and_8_out), .Q(_7_q), .clk(Clock), .clr(Clear));
  and and_8 (and_8_out, decoder_1_out7, RegWrite);
  Register #(.width(18)) _8 (.D(Write_Data), .en(and_9_out), .Q(_8_q), .clk(Clock), .clr(Clear));
  and and_9 (and_9_out, decoder_1_out8, RegWrite);
  and and_10 (and_10_out, decoder_1_out9, RegWrite);
  and and_11 (and_11_out, decoder_1_out10, RegWrite);
  and and_12 (and_12_out, decoder_1_out11, RegWrite);
  and and_13 (and_13_out, decoder_1_out12, RegWrite);
  and and_14 (and_14_out, decoder_1_out13, RegWrite);
  and and_15 (and_15_out, decoder_1_out14, RegWrite);
  and and_16 (and_16_out, decoder_1_out15, RegWrite);
  Register #(.width(18)) _9 (.D(Write_Data), .en(and_10_out), .Q(_9_q), .clk(Clock), .clr(Clear));
  Register #(.width(18)) _10 (.D(Write_Data), .en(and_11_out), .Q(_10_q), .clk(Clock), .clr(Clear));
  Register #(.width(18)) _11 (.D(Write_Data), .en(and_12_out), .Q(_11_q), .clk(Clock), .clr(Clear));
  Register #(.width(18)) _12 (.D(Write_Data), .en(and_13_out), .Q(_12_q), .clk(Clock), .clr(Clear));
  Register #(.width(18)) _13 (.D(Write_Data), .en(and_14_out), .Q(_13_q), .clk(Clock), .clr(Clear));
  Register #(.width(18)) _14 (.D(Write_Data), .en(and_15_out), .Q(_14_q), .clk(Clock), .clr(Clear));
  Register #(.width(18)) _15 (.D(Write_Data), .en(and_16_out), .Q(_15_q), .clk(Clock), .clr(Clear));
  Multiplexer #(.select(4), .width(18), .enable("false")) multiplexer_1 (
    .in0(_0_q), .in1(_1_q), .in2(_2_q), .in3(_3_q), .in4(_4_q), .in5(_5_q), .in6(_6_q), .in7(_7_q),
    .in8(_8_q), .in9(_9_q), .in10(_10_q), .in11(_11_q), .in12(_12_q), .in13(_13_q), .in14(_14_q),
    .in15(_15_q), .out(Read_Register1_RS_2), .sel(Read_Register1_RS));
  Multiplexer #(.select(4), .width(18), .enable("false")) multiplexer_2 (
    .in0(_0_q), .in1(_1_q), .in2(_2_q), .in3(_3_q), .in4(_4_q), .in5(_5_q), .in6(_6_q), .in7(_7_q),
    .in8(_8_q), .in9(_9_q), .in10(_10_q), .in11(_11_q), .in12(_12_q), .in13(_13_q), .in14(_14_q),
    .in15(_15_q), .out(Read_Register2_RT_2), .sel(Read_Register2_RT));
endmodule

module ALU (
  input  [17:0] A,
  input  [17:0] B,
  input  [2:0] Opcode,
  output [17:0] Result,
  output Zero
);

  wire comparator_1_eq;
  wire [17:0] adder_1_out, bit_extender_1_out, nand_1_out, nor_1_out, or_1_out, subtractor_1_out;

  Comparator #(.width(18)) comparator_1 (.a(A), .b(B), .eq(comparator_1_eq));  // open: gt, lt
  Adder #(.width(18)) adder_1 (.a(A), .b(B), .out(adder_1_out));  // open: cin, cout
  assign nand_1_out = ~(A & B);  // NAND_Gate nand_1, 18 bits wide
  assign nor_1_out = ~(A | B);  // NOR_Gate nor_1, 18 bits wide
  assign bit_extender_1_out = {{17{1'b0}}, comparator_1_eq};  // Bit_Extender bit_extender_1
  Subtractor #(.width(18)) subtractor_1 (.a(A), .b(B), .out(subtractor_1_out));  // open: bin, bout
  assign or_1_out = A | B;  // OR_Gate or_1, 18 bits wide
  Multiplexer #(.select(3), .width(18), .enable("false")) multiplexer_1 (
    .in0(adder_1_out), .in1(nand_1_out), .in2(nor_1_out), .in3(bit_extender_1_out), .in4(subtractor_1_out),
    .in5(or_1_out), .out(Result), .sel(Opcode));  // open: in6, in7
  nor nor_2 (Zero, Result[0], Result[1], Result[2], Result[3], Result[4], Result[5], Result[6], Result[7], Result[8], Result[9], Result[10], Result[11], Result[12], Result[13], Result[14], Result[15], Result[16], Result[17]);

  // Notes on the sheet:
  //   000ADD, 001NAND, 010NOR, 011SLT,100SUB,101OR  
endmodule

module ALUControl (
  input  [1:0] ALUop,
  input  [1:0] Func,
  output [2:0] Op
);

  and and_1 (Op[0], ALUop[1], Func[0]);

  assign Op[2:1] = {ALUop[0], Func[1]};
endmodule

module ControlUnit (
  input  [3:0] Opcode,
  output RegDst,
  output ALUSrc,
  output MemtoReg,
  output RegWrite,
  output MemRead,
  output MemWrite,
  output Branch,
  output ALUop1,
  output ALUop0
);

  wire and_2_out, and_3_out, and_9_out, not_1_out, not_2_out, not_3_out, not_4_out, not_5_out, not_6_out,
       not_7_out, not_8_out, not_9_out, not_10_out, not_11_out;

  not not_1 (not_1_out, Opcode[2]);
  not not_2 (not_2_out, Opcode[1]);
  not not_3 (not_3_out, Opcode[0]);
  not not_4 (not_4_out, Opcode[1]);
  not not_5 (not_5_out, Opcode[0]);
  not not_6 (not_6_out, Opcode[1]);
  not not_7 (not_7_out, Opcode[0]);
  not not_8 (not_8_out, Opcode[0]);
  not not_9 (not_9_out, Opcode[2]);
  not not_10 (not_10_out, Opcode[0]);
  not not_11 (not_11_out, Opcode[2]);
  and and_1 (RegDst, not_1_out, not_2_out, not_3_out);
  and and_2 (and_2_out, not_4_out, Opcode[0]);
  and and_3 (and_3_out, Opcode[1], not_5_out);
  and and_4 (RegWrite, not_6_out, not_7_out);
  and and_5 (MemRead, Opcode[2], not_8_out);
  and and_6 (MemWrite, Opcode[2], Opcode[0]);
  and and_7 (Branch, Opcode[1], Opcode[0]);
  and and_8 (ALUop1, not_9_out, not_10_out);
  and and_9 (and_9_out, not_11_out, Opcode[0]);
  or or_1 (ALUSrc, and_2_out, and_3_out, Opcode[2]);
  or or_2 (ALUop0, and_9_out, Opcode[1]);

  assign MemtoReg = Opcode[2];
endmodule

module ALUControlUpdated (
  input  [1:0] ALUop,
  input  [1:0] Func,
  output [2:0] Op
);

  wire and_1_out, and_2_out, and_3_out, not_1_out, not_2_out, not_3_out;

  not not_1 (not_1_out, ALUop[1]);
  not not_2 (not_2_out, ALUop[0]);
  not not_3 (not_3_out, ALUop[0]);
  and and_1 (and_1_out, not_1_out, ALUop[0]);
  and and_2 (and_2_out, ALUop[1], not_2_out);
  and and_3 (and_3_out, ALUop[1], not_3_out);
  or or_1 (Op[2], and_1_out, and_2_out);
  or or_2 (Op[0], Func[0], and_3_out);

  assign Op[1] = Func[1];
endmodule

module ControlUnitUpdated (
  input  [3:0] Opcode,
  output RegDst,
  output ALUSrc,
  output MemtoReg,
  output RegWrite,
  output MemRead,
  output MemWrite,
  output Branch,
  output ALUop1,
  output ALUop2
);

  wire and_2_out, and_3_out, and_9_out, and_10_out, not_1_out, not_2_out, not_3_out, not_4_out, not_5_out,
       not_6_out, not_7_out, not_8_out, not_9_out, not_10_out, not_11_out, not_12_out, not_13_out;

  not not_1 (not_1_out, Opcode[2]);
  and and_1 (RegDst, not_1_out, not_2_out, not_3_out);
  not not_2 (not_2_out, Opcode[1]);
  not not_3 (not_3_out, Opcode[0]);
  not not_4 (not_4_out, Opcode[1]);
  and and_2 (and_2_out, not_4_out, Opcode[0]);
  and and_3 (and_3_out, Opcode[1], not_5_out);
  not not_5 (not_5_out, Opcode[0]);
  not not_6 (not_6_out, Opcode[1]);
  and and_4 (RegWrite, not_6_out, not_7_out);
  not not_7 (not_7_out, Opcode[0]);
  and and_5 (MemRead, Opcode[2], not_8_out);
  not not_8 (not_8_out, Opcode[0]);
  and and_6 (MemWrite, Opcode[2], Opcode[0]);
  and and_7 (Branch, Opcode[1], Opcode[0]);
  not not_9 (not_9_out, Opcode[2]);
  and and_8 (ALUop1, not_9_out, not_10_out);
  not not_10 (not_10_out, Opcode[0]);
  not not_11 (not_11_out, Opcode[2]);
  and and_9 (and_9_out, not_11_out, not_12_out);
  not not_12 (not_12_out, Opcode[1]);
  not not_13 (not_13_out, Opcode[2]);
  and and_10 (and_10_out, not_13_out, Opcode[0]);
  or or_1 (ALUSrc, and_2_out, and_3_out, Opcode[2]);
  or or_2 (ALUop2, and_9_out, and_10_out);

  assign MemtoReg = Opcode[2];
endmodule
